// Logisim project 10_2.circ as structural Verilog: 1 circuit, main circuit main
module main (
);

  wire and_1_out, and_2_out, and_3_out, and_4_out, and_5_out, or_1_out, undriven, undriven_2, undriven_3,
       undriven_4, undriven_5, undriven_6, undriven_7, undriven_8, xor_1_out, xor_2_out, xor_3_out,
       xor_4_out, xor_5_out, xor_6_out, xor_7_out, xor_8_out, xor_9_out;

  xor xor_1 (xor_1_out, undriven, undriven_2);
  xor xor_2 (xor_2_out, undriven_3, undriven_4);
  xor xor_3 (xor_3_out, undriven_5, undriven_6);
  xor xor_4 (xor_4_out, undriven_7, undriven_8);
  and and_1 (and_1_out, xor_1_out, xor_2_out);
  xor xor_5 (xor_5_out, xor_1_out, xor_2_out);
  and and_2 (and_2_out, xor_3_out, xor_4_out);
  xor xor_6 (xor_6_out, xor_3_out, xor_4_out);
  and and_3 (and_3_out, and_1_out, and_2_out);
  xor xor_7 (xor_7_out, and_1_out, and_2_out);
  and and_4 (and_4_out, xor_5_out, xor_6_out);
  xor xor_8 (xor_8_out, xor_5_out, xor_6_out);
  or or_1 (or_1_out, and_3_out, and_5_out);
  and and_5 (and_5_out, xor_7_out, and_4_out);
  xor xor_9 (xor_9_out, xor_7_out, and_4_out);

  // Notes on the sheet:
  //   a_1
  //   b_1
  //   a_2
  //   b_2
  //   a_3
  //   b_3
  //   a_4
  //   b_4
  //   c_3
  //   c_2
  //   c_1
endmodule
