// Logisim project 10_3.circ as structural Verilog: 1 circuit, main circuit main
module main (
  input  in_1,
  input  in_2,
  input  in_3,
  input  in_4,
  input  in_5,
  input  in_6,
  input  in_7
);

  wire decoder_1_out1, decoder_1_out2, decoder_1_out3, decoder_1_out4, decoder_1_out5, decoder_1_out6,
       decoder_1_out7, xor_1_out, xor_2_out, xor_3_out, xor_4_out, xor_5_out, xor_6_out, xor_10_out,
       xor_11_out, xor_12_out, xor_13_out, xor_14_out, xor_15_out, xor_16_out;
  wire [2:0] xor_7_out;

  xor xor_1 (xor_1_out, in_3, in_5);
  xor xor_2 (xor_2_out, in_3, in_6);
  xor xor_3 (xor_3_out, in_5, in_6);
  xor xor_4 (xor_4_out, xor_1_out, in_7);
  xor xor_5 (xor_5_out, xor_2_out, in_7);
  xor xor_6 (xor_6_out, xor_3_out, in_7);
  xor xor_7 (xor_7_out[0], xor_4_out, in_1);
  xor xor_8 (xor_7_out[1], xor_5_out, in_2);
  xor xor_9 (xor_7_out[2], xor_6_out, in_4);
  Decoder #(.select(3), .enable("false")) decoder_1 (
    .out1(decoder_1_out1), .out2(decoder_1_out2), .out3(decoder_1_out3), .out4(decoder_1_out4),
    .out5(decoder_1_out5), .out6(decoder_1_out6), .out7(decoder_1_out7), .sel(xor_7_out));  // open: out0
  // Probe on xor_10_out
  xor xor_10 (xor_10_out, decoder_1_out1, in_1);
  // Probe on xor_11_out
  xor xor_11 (xor_11_out, decoder_1_out2, in_2);
  xor xor_12 (xor_12_out, decoder_1_out3, in_3);
  // Probe on xor_12_out
  // Probe on xor_13_out
  xor xor_13 (xor_13_out, decoder_1_out4, in_4);
  xor xor_14 (xor_14_out, decoder_1_out5, in_5);
  // Probe on xor_14_out
  // Probe on xor_15_out
  xor xor_15 (xor_15_out, decoder_1_out6, in_6);
  // Probe on xor_16_out
  xor xor_16 (xor_16_out, decoder_1_out7, in_7);

  // Notes on the sheet:
  //   d1
  //   p3
  //   p1
  //   p2
  //   d2
  //   d3
  //   d4
  //   p1
  //   p2
  //   d1
  //   p3
  //   d2
  //   d3
  //   d4
endmodule
