// Logisim project 10_4.circ as structural Verilog: 1 circuit, main circuit main
module main (
  input  Karte_a,
  input  Taste_a,
  input  Karte_b,
  input  Taste_b,
  input  Karte_c,
  input  Taste_c,
  input  \Zurücksetzen 
);

  wire and_1_out, and_2_out, or_1_out, or_2_out, or_3_out, s_r_ff_1_q, s_r_ff_2_q, s_r_ff_3_q;

  or or_1 (or_1_out, Taste_a, \Zurücksetzen );
  S_R_Flip_Flop s_r_ff_1 (
    .S(Karte_a), .clk(or_1_out), .R(\Zurücksetzen ), .Q(s_r_ff_1_q));  // open: Qn, preset, reset, en
  and and_1 (and_1_out, s_r_ff_1_q, Karte_b);
  or or_2 (or_2_out, Taste_b, \Zurücksetzen );
  S_R_Flip_Flop s_r_ff_2 (
    .S(and_1_out), .clk(or_2_out), .R(\Zurücksetzen ), .Q(s_r_ff_2_q));  // open: Qn, preset, reset, en
  and and_2 (and_2_out, s_r_ff_2_q, Karte_c);
  or or_3 (or_3_out, Taste_c, \Zurücksetzen );
  // Probe on s_r_ff_3_q
  S_R_Flip_Flop s_r_ff_3 (
    .S(and_2_out), .clk(or_3_out), .R(\Zurücksetzen ), .Q(s_r_ff_3_q));  // open: Qn, preset, reset, en
endmodule
