// Logisim project 11.4.3.circ as structural Verilog: 1 circuit, main circuit main
module main (
  input  Leitung_24,
  input  Leitung_23,
  input  Leitung_22,
  input  Leitung_21,
  input  Leitung_20,
  input  Leitung_19,
  input  Leitung_18,
  input  Leitung_17,
  input  Leitung_16,
  input  Leitung_15,
  input  Leitung_14,
  input  Leitung_13,
  input  Leitung_12,
  input  Leitung_11,
  input  Leitung_10,
  input  Leitung_9,
  input  Leitung_8,
  input  Leitung_7,
  input  Leitung_6,
  input  Leitung_5,
  input  Leitung_4,
  input  Leitung_3,
  input  Leitung_2,
  input  Leitung_1
);

  wire and_1_out, and_2_out, and_3_out, and_4_out;

  and and_1 (and_1_out, ~Leitung_21, ~Leitung_22, ~Leitung_23, ~Leitung_24);  // AND_Gate
  // Probe on and_1_out
  and and_2 (and_2_out, Leitung_21, ~Leitung_22, ~Leitung_23, ~Leitung_24);  // AND_Gate
  // Probe on and_2_out
  and and_3 (and_3_out, ~Leitung_21, Leitung_22, ~Leitung_23, ~Leitung_24);  // AND_Gate
  // Probe on and_3_out
  and and_4 (and_4_out, Leitung_21, Leitung_22, ~Leitung_23, ~Leitung_24);  // AND_Gate
  // Probe on and_4_out
  // Probe on Leitung_24
endmodule
