// Logisim project 8.3.circ as structural Verilog: 1 circuit, main circuit main
module main (
);

  wire and_1_out, and_2_out, and_3_out, and_4_out, or_1_out, undriven, undriven_2, undriven_3;

  and and_1 (and_1_out, ~undriven, undriven_2, ~undriven_3);  // AND_Gate
  and and_2 (and_2_out, ~undriven, undriven_2, undriven_3);  // AND_Gate
  or or_1 (or_1_out, and_1_out, and_2_out, and_3_out, and_4_out);
  and and_3 (and_3_out, undriven, ~undriven_2, undriven_3);  // AND_Gate
  and and_4 (and_4_out, undriven, undriven_2, undriven_3);

  // Notes on the sheet:
  //   a
  //   b
  //   c
  //   r
endmodule
